# Fritzing sketch Moisture Sensor (saved by Fritzing 0.9.3b)
breadboards: 1

parts:
  Part1 = Arduino Uno (Rev3)
  Part2 = Soil Moisture Sensor
  R1 = Resistor [tolerance=±5% resistance=220 package=THT]
  LED1 = LED - 5mm [color="Red (633nm)" package="5 mm [THT]"]

nets:
  N1: Part1.A0, Part2.SIG
  N2: Part1.D8, LED1.anode
  GND: Part1.GND, Part2.GND, R1.Pin_0
  5V: Part1.5V, Part2.VCC
  N3: R1.Pin_1, LED1.cathode
